// Logisim project Cache.circ as structural Verilog
module implementation (
  input  [9:0] CpuAddressIn,
  input  CpuReadIn,
  input  CpuWriteIn,
  input  [7:0] CpuWriteValueIn,
  input  [31:0] LineFromMemIn,
  input  ClkIn,
  output ReadyOut,
  output DidContainOut,
  output [7:0] ByteReadOut,
  output [7:0] MemAddressOut,
  output MemReadOut,
  output MemWriteOut,
  output [31:0] Line2MemOut
);


  // Other names for the same wires on the sheet: clk = ClkIn; CpuAddress[9:0] = CpuAddressIn; CpuRead = CpuReadIn;
  //   CpuWrite = CpuWriteIn; CpuWriteValue[7:0] = CpuWriteValueIn; DidContain = DidContainOut;
  //   LineFromMem[31:0] = LineFromMemIn; MemAddress[7:0] = MemAddressOut; MemRead = MemReadOut;
  //   MemWrite = MemWriteOut; Ready = ReadyOut; ByteRead[7:0] = ByteReadOut; SelectedSetByteRead[7:0] = ByteReadOut;
  //   Line2Mem[31:0] = Line2MemOut; SelectedSetLine2Mem[31:0] = Line2MemOut
endmodule

module Cache (
  input  [9:0] CpuAddressIn,
  input  CpuReadIn,
  input  CpuWriteIn,
  input  [7:0] CpuWriteValueIn,
  input  [31:0] LineFromMemIn,
  input  ClkIn,
  output ReadyOut,
  output DidContainOut,
  output [7:0] ByteReadOut,
  output [7:0] MemAddressOut,
  output MemReadOut,
  output MemWriteOut,
  output [31:0] Line2MemOut
);

  wire CacheActive, CpuReadIn_t, CpuWriteIn_t, Initialize, not_2_out, SetBits, StoredCpuRead, StoredCpuWrite;
  wire [1:0] BlockBits;
  wire [7:0] StoredCpuWriteValue;
  wire [9:3] StoredCpuAddress;

  Register #(.width(10)) register_1 (
    .D(CpuAddressIn), .en(Initialize), .clk(ClkIn), .Q({StoredCpuAddress, SetBits, BlockBits}));  // open: clr
  Register #(.width(1)) register_2 (.D(CpuReadIn), .en(Initialize), .clk(ClkIn), .Q(StoredCpuRead));  // open: clr
  Register #(.width(1)) register_3 (.D(CpuWriteIn), .en(Initialize), .clk(ClkIn), .Q(StoredCpuWrite));  // open: clr
  Register register_4 (.D(CpuWriteValueIn), .en(Initialize), .clk(ClkIn), .Q(StoredCpuWriteValue));  // open: clr
  Multiplexer #(.enable("false")) multiplexer_1 (
    .in0(StoredCpuRead), .in1(CpuReadIn), .out(CpuReadIn_t), .sel(Initialize));
  Multiplexer #(.enable("false")) multiplexer_2 (
    .in0(StoredCpuWrite), .in1(CpuWriteIn), .out(CpuWriteIn_t), .sel(Initialize));
  not not_1 (CacheActive, ReadyOut);
  // AND_Gate and_1 has open pins: in0=CacheActive, in1=not_2_out, out=open
  not not_2 (not_2_out, SetBits);
  FSMController fsmcontroller_1 (
    .Read(CpuReadIn_t), .Write(CpuWriteIn_t), .Ready(ReadyOut), .Initialize(Initialize),
    .MemReadOut(MemReadOut), .MemWriteOut(MemWriteOut));  // open: didContain, Dirty
  Set set0 ();  // open: Active, BlockBits, TagBits, CpuReadIn, CpuWriteIn, CpuWriteValueIn, LineFromMemIn, ClkIn, DidContainOut, ByteReadOut, MemAddressOut, Line2MemOut
  Set set1 ();  // open: Active, BlockBits, TagBits, CpuReadIn, CpuWriteIn, CpuWriteValueIn, LineFromMemIn, ClkIn, DidContainOut, ByteReadOut, MemAddressOut, Line2MemOut

  // Other names for the same wires on the sheet: ByteRead[7:0] = ByteReadOut; clk = ClkIn;
  //   CpuAddress[9:0] = CpuAddressIn; CpuRead = CpuReadIn; CpuWrite = CpuWriteIn;
  //   CpuWriteValue[7:0] = CpuWriteValueIn; DidContain = DidContainOut; Line2Mem[31:0] = Line2MemOut;
  //   LineFromMem[31:0] = LineFromMemIn; MemAddress[7:0] = MemAddressOut; MemRead = MemReadOut;
  //   MemWrite = MemWriteOut; Ready = ReadyOut; StoredCpuAddress[2:0] = {SetBits, BlockBits};
  //   TagBits[6:0] = StoredCpuAddress
endmodule

module Set (
  input  Active,
  input  BlockBits,
  input  TagBits,
  input  CpuReadIn,
  input  CpuWriteIn,
  input  [7:0] CpuWriteValueIn,
  input  [31:0] LineFromMemIn,
  input  ClkIn,
  output DidContainOut,
  output [7:0] ByteReadOut,
  output [7:0] MemAddressOut,
  output [31:0] Line2MemOut
);


  // Other names for the same wires on the sheet: ByteRead[7:0] = ByteReadOut; clk = ClkIn; CpuRead = CpuReadIn;
  //   CpuWrite = CpuWriteIn; CpuWriteValue[7:0] = CpuWriteValueIn; DidContain = DidContainOut;
  //   Line2Mem[31:0] = Line2MemOut; LineFromMem[31:0] = LineFromMemIn; MemAddress[7:0] = MemAddressOut
endmodule

module FSMController (
  input  Read,
  input  Write,
  input  didContain,
  input  Dirty,
  output Ready,
  output Initialize,
  output MemReadOut,
  output MemWriteOut
);

  wire [2:0] nextstate_1_nextstate, register_1_q;

  NextState nextstate_1 (
    .CurrentState(register_1_q), .Read(Read), .Write(Write), .didContain(didContain), .Dirty(Dirty),
    .NextState(nextstate_1_nextstate));
  Register #(.width(3)) register_1 (.D(nextstate_1_nextstate), .Q(register_1_q));  // open: en, clk, clr
  FSMOutput fsmoutput_1 (
    .State(register_1_q), .Ready(Ready), .Initialize(Initialize), .MemReadOut(MemReadOut),
    .MemWriteOut(MemWriteOut));
endmodule

module FSMOutput (
  input  [2:0] State,
  output Ready,
  output Initialize,
  output MemReadOut,
  output MemWriteOut
);

  wire not_1_out, not_2_out, not_3_out;

  not not_1 (not_1_out, State[2]);
  not not_2 (not_2_out, State[1]);
  not not_3 (not_3_out, State[0]);
  and and_1 (Ready, not_1_out, not_2_out, not_3_out);
  and and_2 (Initialize, not_1_out, not_2_out, not_3_out);
  and and_3 (MemReadOut, State[2], State[1], not_3_out);
  and and_4 (MemWriteOut, not_1_out, State[1], not_3_out);
endmodule

module NextState (
  input  [2:0] CurrentState,
  input  Read,
  input  Write,
  input  didContain,
  input  Dirty,
  output [2:0] NextState
);

  wire and_1_out, and_2_out, and_3_out, and_4_out, and_5_out, and_6_out, and_7_out, and_8_out, and_9_out,
       and_10_out, not_1_out, not_2_out, not_3_out, not_4_out, not_5_out, not_6_out;

  not not_1 (not_1_out, CurrentState[2]);
  not not_2 (not_2_out, CurrentState[1]);
  not not_3 (not_3_out, CurrentState[0]);
  not not_4 (not_4_out, Read);
  not not_5 (not_5_out, didContain);
  not not_6 (not_6_out, Dirty);
  and and_1 (and_1_out, not_2_out, CurrentState[0], not_5_out, not_6_out);
  and and_2 (and_2_out, not_2_out, CurrentState[0], not_4_out, didContain);
  and and_3 (and_3_out, CurrentState[1], not_3_out);
  and and_4 (and_4_out, CurrentState[2], not_3_out, not_4_out);
  and and_5 (and_5_out, not_2_out, CurrentState[0]);
  and and_6 (and_6_out, not_1_out, CurrentState[1], not_3_out);
  or or_1 (NextState[1], and_5_out, and_6_out, and_7_out);
  and and_7 (and_7_out, CurrentState[2], not_2_out);
  and and_8 (and_8_out, not_2_out, not_3_out, Write);
  and and_9 (and_9_out, not_2_out, not_3_out, Read);
  or or_2 (NextState[0], and_8_out, and_9_out, and_10_out);
  and and_10 (and_10_out, not_2_out, CurrentState[0], didContain);
  or or_3 (NextState[2], and_1_out, and_2_out, and_3_out, and_4_out);
endmodule
